# Fritzing sketch schematics (saved by Fritzing 0.9.2b)
circuit board: 8.46667cm x 5.64444cm

parts:
  S1 = Round Pushbutton
  Raspberry_Pi1 = Raspberry Pi 2
  LED1 = smd LED [color="Red (633nm)" package="0603 [SMD]"]
  R1 = Resistor [tolerance=±5% resistance=330 package="0805 [SMD]"]

nets:
  N1: S1.leg0, Raspberry_Pi1.GPIO4
  N2: S1.leg1, Raspberry_Pi1.3v3
  N3: Raspberry_Pi1.GPIO27, R1.Pin_1
  N4: Raspberry_Pi1.GND, LED1.cathode
  N5: LED1.anode, R1.Pin_0
